// Logisim project cpu_250.circ as structural Verilog: 15 circuits, main circuit main
module main (
  input  reset
);

  wire AddOrSub, ALUinB, Ble, Bne, clk, DMwe, InE, Jale, Jp, Jre, keyboard_1_avail, LessThan, LessThanEnable,
       memory_latch_1_oe_latched, memory_latch_1_we_latched, not_1_out, not_2_out, not_4_out, NotEqualTo,
       NotEqualToEnable, OutE, Rdst, Rwd, Rwe;
  wire [2:0] ALUOp, multiplexer_4_out, multiplexer_6_out, Rd, Rs, Rt, Shamt;
  wire [3:0] Opcode;
  wire [5:0] Imm;
  wire [6:0] bit_extender_1_out;
  wire [7:0] KeyboardRtIn;
  wire [11:0] Address;
  wire [15:0] Address16Bit, addsub_1_result, addsub_2_result, ALUOut, BrImm, memory_latch_1_address_latched,
       memory_latch_1_data_in_latched, multiplexer_1_out, multiplexer_2_out, multiplexer_3_out,
       multiplexer_5_out, multiplexer_7_out, multiplexer_8_out, multiplexer_10_out, multiplexer_11_out,
       OutputRs, PC_out_5, PCNext, PCPlus1, ram_1_dout, rom_1_data, swImm;

  Clock clock_1 (.out(clk));
  not not_1 (not_1_out, clk);
  PCAdder pcadder_1 (.PCout(PCPlus1), .PCin(PC_out_5));
  Keyboard keyboard_1 (.clk(not_1_out), .re(InE), .clr(reset), .avail(keyboard_1_avail), .data(KeyboardRtIn[6:0]));
  Reg PC (.RegIn(PCNext), .RegReset(reset), .out_5(PC_out_5), .clk(not_2_out), .WE(1'b1));
  not not_2 (not_2_out, clk);
  not not_3 (KeyboardRtIn[7], keyboard_1_avail);
  ROM #(.addrWidth(16), .dataWidth(16)) rom_1 (.addr(PC_out_5), .data(rom_1_data));
  // Probe on PC_out_5
  Bit_Extender #(.in_width(16), .out_width(7)) bit_extender_1 (.in(OutputRs), .out(bit_extender_1_out));
  AddSub addsub_1 (.sub(1'b0), .B(PCPlus1), .A(BrImm), .result(addsub_1_result));  // open: ovf
  AddSub addsub_2 (.sub(1'b0), .B(PCPlus1), .A(BrImm), .result(addsub_2_result));  // open: ovf
  and and_1 (NotEqualToEnable, Bne, NotEqualTo);
  and and_2 (LessThanEnable, Ble, LessThan);
  TTY #(.rows(13), .cols(80)) tty_1 (.data(bit_extender_1_out), .clk(clk), .we(OutE), .clr(reset));
  Multiplexer #(.width(16), .enable("false")) multiplexer_1 (
    .in0(PCPlus1), .in1(addsub_1_result), .out(multiplexer_1_out), .sel(LessThanEnable));
  Multiplexer #(.width(16), .enable("false")) multiplexer_2 (
    .in0(multiplexer_1_out), .in1(addsub_2_result), .out(multiplexer_2_out), .sel(NotEqualToEnable));
  InstructionDecoder instructiondecoder_1 (
    .InstructionIn(rom_1_data), .Opcode(Opcode), .Rs(Rs), .Rt(Rt), .Address(Address), .Rd(Rd), .Imm(Imm),
    .Shamt(Shamt));
  // Probe on Opcode
  // Probe on Rs
  // Probe on Rt
  // Probe on Address
  // Probe on Rd
  // Probe on Imm
  // Probe on Shamt
  Multiplexer #(.width(16), .enable("false")) multiplexer_3 (
    .in0(multiplexer_5_out), .in1({{8{1'b0}}, KeyboardRtIn}), .out(multiplexer_3_out), .sel(InE));
  // Probe on multiplexer_3_out
  Multiplexer #(.width(3), .enable("false")) multiplexer_4 (.in0(Rt), .in1(Rd), .out(multiplexer_4_out), .sel(Rdst));
  assign Address16Bit = {{4{1'b0}}, Address};  // Bit_Extender bit_extender_2
  Multiplexer #(.width(16), .enable("false")) multiplexer_5 (
    .in0(multiplexer_11_out), .in1(PCPlus1), .out(multiplexer_5_out), .sel(Jale));
  Multiplexer #(.width(3), .enable("false")) multiplexer_6 (
    .in0(multiplexer_4_out), .in1(3'b111), .out(multiplexer_6_out), .sel(Jale));
  // Probe on multiplexer_6_out
  Multiplexer #(.width(16), .enable("false")) multiplexer_7 (
    .in0(multiplexer_2_out), .in1(Address16Bit), .out(multiplexer_7_out), .sel(Jp));
  Multiplexer #(.width(16), .enable("false")) multiplexer_8 (
    .in0(multiplexer_7_out), .in1(OutputRs), .out(multiplexer_8_out), .sel(Jre));
  Multiplexer #(.width(16), .enable("false")) multiplexer_9 (
    .in0(multiplexer_8_out), .in1(Address16Bit), .out(PCNext), .sel(Jale));
  RegisterFile registerfile_1 (
    .ReadReg2(Rt), .clk(clk), .Reset(reset), .WriteReg(multiplexer_6_out), .RegWriteEnable(Rwe),
    .WriteData(multiplexer_3_out), .ReadReg1(Rs), .ReadData1(OutputRs), .ReadData2(swImm));
  Control control_1 (
    .ALUinB(ALUinB), .ALUOp(ALUOp), .Rdst(Rdst), .Rwe(Rwe), .Opcode(Opcode), .AddOrSub(AddOrSub),
    .DMwe(DMwe), .Rwd(Rwd), .JP(Jp), .bne(Bne), .Jre(Jre), .Jale(Jale), .InE(InE), .OutE(OutE), .ble(Ble));
  // Probe on multiplexer_11_out
  assign BrImm = {{10{Imm[5]}}, Imm};  // Bit_Extender bit_extender_3
  // Probe on OutputRs
  Multiplexer #(.width(16), .enable("false")) multiplexer_10 (
    .in0(swImm), .in1(BrImm), .out(multiplexer_10_out), .sel(ALUinB));
  ALU alu_1 (
    .SubSelect(AddOrSub), .B(multiplexer_10_out), .A(OutputRs), .ALUop(ALUOp), .ShiftBit(Shamt),
    .ALUOut(ALUOut), .NotEqual(NotEqualTo), .Less(LessThan));
  not not_4 (not_4_out, clk);
  RAM #(.addrWidth(16), .dataWidth(16), .trigger("high"), .databus("bibus")) ram_1 (
    .addr(memory_latch_1_address_latched), .we(memory_latch_1_we_latched), .oe(memory_latch_1_oe_latched),
    .din(memory_latch_1_data_in_latched), .dout(ram_1_dout));
  memory_latch memory_latch_1 (
    .address(ALUOut), .WE(DMwe), .clk(not_4_out), .data_in(swImm),
    .address_latched(memory_latch_1_address_latched), .WE_latched(memory_latch_1_we_latched),
    .OE_latched(memory_latch_1_oe_latched), .data_in_latched(memory_latch_1_data_in_latched));
  Multiplexer #(.width(16), .enable("false")) multiplexer_11 (
    .in0(ALUOut), .in1(ram_1_dout), .out(multiplexer_11_out), .sel(Rwd));

  // Other names for the same wires on the sheet: RsVal[15:0] = OutputRs
endmodule

module Reg (
  input  [15:0] RegIn,
  input  WE,
  input  clk,
  input  RegReset,
  output [15:0] out_5
);

  wire clk_t;

  and and_1 (clk_t, WE, clk);
  D_Flip_Flop d_ff_1 (.D(RegIn[0]), .clk(clk_t), .Q(out_5[0]), .reset(RegReset));  // open: Qn, preset
  D_Flip_Flop d_ff_2 (.D(RegIn[1]), .clk(clk_t), .Q(out_5[1]), .reset(RegReset));  // open: Qn, preset
  D_Flip_Flop d_ff_3 (.D(RegIn[2]), .clk(clk_t), .Q(out_5[2]), .reset(RegReset));  // open: Qn, preset
  D_Flip_Flop d_ff_4 (.D(RegIn[3]), .clk(clk_t), .Q(out_5[3]), .reset(RegReset));  // open: Qn, preset
  D_Flip_Flop d_ff_5 (.D(RegIn[4]), .clk(clk_t), .Q(out_5[4]), .reset(RegReset));  // open: Qn, preset
  D_Flip_Flop d_ff_6 (.D(RegIn[5]), .clk(clk_t), .Q(out_5[5]), .reset(RegReset));  // open: Qn, preset
  D_Flip_Flop d_ff_7 (.D(RegIn[6]), .clk(clk_t), .Q(out_5[6]), .reset(RegReset));  // open: Qn, preset
  D_Flip_Flop d_ff_8 (.D(RegIn[7]), .clk(clk_t), .Q(out_5[7]), .reset(RegReset));  // open: Qn, preset
  D_Flip_Flop d_ff_9 (.D(RegIn[8]), .clk(clk_t), .Q(out_5[8]), .reset(RegReset));  // open: Qn, preset
  D_Flip_Flop d_ff_10 (.D(RegIn[9]), .clk(clk_t), .Q(out_5[9]), .reset(RegReset));  // open: Qn, preset
  D_Flip_Flop d_ff_11 (.D(RegIn[10]), .clk(clk_t), .Q(out_5[10]), .reset(RegReset));  // open: Qn, preset
  D_Flip_Flop d_ff_12 (.D(RegIn[11]), .clk(clk_t), .Q(out_5[11]), .reset(RegReset));  // open: Qn, preset
  D_Flip_Flop d_ff_13 (.D(RegIn[12]), .clk(clk_t), .Q(out_5[12]), .reset(RegReset));  // open: Qn, preset
  D_Flip_Flop d_ff_14 (.D(RegIn[13]), .clk(clk_t), .Q(out_5[13]), .reset(RegReset));  // open: Qn, preset
  D_Flip_Flop d_ff_15 (.D(RegIn[14]), .clk(clk_t), .Q(out_5[14]), .reset(RegReset));  // open: Qn, preset
  D_Flip_Flop d_ff_16 (.D(RegIn[15]), .clk(clk_t), .Q(out_5[15]), .reset(RegReset));  // open: Qn, preset
endmodule

module RegisterFile (
  input  [15:0] WriteData,
  input  Reset,
  input  clk,
  input  RegWriteEnable,
  input  [2:0] ReadReg1,
  input  [2:0] WriteReg,
  input  [2:0] ReadReg2,
  output [15:0] ReadData1,
  output [15:0] ReadData2
);

  wire decoder_3_out0, decoder_3_out1, decoder_3_out2, decoder_3_out3, decoder_3_out4, decoder_3_out5,
       decoder_3_out6, decoder_3_out7, Read1R0, Read1R1, Read1R2, Read1R3, Read1R4, Read1R5, Read1R6,
       Read1R7, Read2R0, Read2R1, Read2R2, Read2R3, Read2R4, Read2R5, Read2R6, Read2R7, RegReset, WriteR0,
       WriteR1, WriteR2, WriteR3, WriteR4, WriteR5, WriteR6, WriteR7;
  wire [15:0] R0, R1, R2, R3, R4, R5, R6, R7;

  Decoder #(.select(3)) decoder_1 (
    .out0(Read1R0), .out1(Read1R1), .out2(Read1R2), .out3(Read1R3), .out4(Read1R4), .out5(Read1R5),
    .out6(Read1R6), .out7(Read1R7), .sel(ReadReg1));  // open: en
  Decoder #(.select(3)) decoder_2 (
    .out0(Read2R0), .out1(Read2R1), .out2(Read2R2), .out3(Read2R3), .out4(Read2R4), .out5(Read2R5),
    .out6(Read2R6), .out7(Read2R7), .sel(ReadReg2));  // open: en
  // Probe on WriteData
  Decoder #(.select(3)) decoder_3 (
    .out0(decoder_3_out0), .out1(decoder_3_out1), .out2(decoder_3_out2), .out3(decoder_3_out3),
    .out4(decoder_3_out4), .out5(decoder_3_out5), .out6(decoder_3_out6), .out7(decoder_3_out7), .sel(WriteReg));  // open: en
  Reg reg_1 (.RegIn(WriteData), .RegReset(RegReset), .out_5(R0), .clk(clk));  // open: WE
  // Probe on R0
  Reg reg_2 (.RegIn(WriteData), .RegReset(RegReset), .out_5(R1), .clk(clk), .WE(WriteR1));
  // Probe on R1
  Reg reg_3 (.RegIn(WriteData), .RegReset(RegReset), .out_5(R2), .clk(clk), .WE(WriteR2));
  // Probe on R2
  Reg reg_4 (.RegIn(WriteData), .RegReset(RegReset), .out_5(R3), .clk(clk), .WE(WriteR3));
  // Probe on R3
  Reg reg_5 (.RegIn(WriteData), .RegReset(RegReset), .out_5(R4), .clk(clk), .WE(WriteR4));
  // Probe on R4
  Reg reg_6 (.RegIn(WriteData), .RegReset(RegReset), .out_5(R5), .clk(clk), .WE(WriteR5));
  // Probe on R5
  Reg reg_7 (.RegIn(WriteData), .RegReset(RegReset), .out_5(R6), .clk(clk), .WE(WriteR6));
  // Probe on R6
  Reg reg_8 (.RegIn(WriteData), .RegReset(RegReset), .out_5(R7), .clk(clk), .WE(WriteR7));
  // Probe on R7
  and and_1 (WriteR0, RegWriteEnable, decoder_3_out0);
  and and_2 (WriteR1, RegWriteEnable, decoder_3_out1);
  and and_3 (WriteR2, RegWriteEnable, decoder_3_out2);
  and and_4 (WriteR3, RegWriteEnable, decoder_3_out3);
  and and_5 (WriteR4, decoder_3_out4, RegWriteEnable);
  and and_6 (WriteR5, decoder_3_out5, RegWriteEnable);
  and and_7 (WriteR6, decoder_3_out6, RegWriteEnable);
  and and_8 (WriteR7, decoder_3_out7, RegWriteEnable);
  assign ReadData1 = Read1R0 ? R0 : 16'bz;  // Controlled_Buffer controlled_buffer_1
  assign ReadData1 = Read1R1 ? R1 : 16'bz;  // Controlled_Buffer controlled_buffer_2
  assign ReadData1 = Read1R2 ? R2 : 16'bz;  // Controlled_Buffer controlled_buffer_3
  assign ReadData1 = Read1R3 ? R3 : 16'bz;  // Controlled_Buffer controlled_buffer_4
  assign ReadData1 = Read1R4 ? R4 : 16'bz;  // Controlled_Buffer controlled_buffer_5
  assign ReadData1 = Read1R5 ? R5 : 16'bz;  // Controlled_Buffer controlled_buffer_6
  assign ReadData1 = Read1R6 ? R6 : 16'bz;  // Controlled_Buffer controlled_buffer_7
  assign ReadData1 = Read1R7 ? R7 : 16'bz;  // Controlled_Buffer controlled_buffer_8
  assign ReadData2 = Read2R0 ? R0 : 16'bz;  // Controlled_Buffer controlled_buffer_9
  assign ReadData2 = Read2R1 ? R1 : 16'bz;  // Controlled_Buffer controlled_buffer_10
  assign ReadData2 = Read2R2 ? R2 : 16'bz;  // Controlled_Buffer controlled_buffer_11
  assign ReadData2 = Read2R3 ? R3 : 16'bz;  // Controlled_Buffer controlled_buffer_12
  assign ReadData2 = Read2R4 ? R4 : 16'bz;  // Controlled_Buffer controlled_buffer_13
  assign ReadData2 = Read2R5 ? R5 : 16'bz;  // Controlled_Buffer controlled_buffer_14
  assign ReadData2 = Read2R6 ? R6 : 16'bz;  // Controlled_Buffer controlled_buffer_15
  assign ReadData2 = Read2R7 ? R7 : 16'bz;  // Controlled_Buffer controlled_buffer_16

  // Other names for the same wires on the sheet: RegWE = RegWriteEnable
endmodule

module ALU (
  input  SubSelect,
  input  [15:0] B,
  input  [15:0] A,
  input  [2:0] ALUop,
  input  [2:0] ShiftBit,
  output [15:0] ALUOut,
  output NotEqual,
  output Less
);

  wire [15:0] addsub_1_result, and_1_out, not_1_out, shiftleft_1_shiftout, shiftright_1_shiftout;

  assign and_1_out = A & B;  // AND_Gate and_1, 16 bits wide
  assign not_1_out = ~A;  // NOT_Gate not_1, 16 bits wide
  NotEqualTo notequalto_1 (.NotEqual(NotEqual), .B(B), .A(A));
  LessThan lessthan_1 (.Neg(Less), .B(B), .A(A));
  ShiftLeft shiftleft_1 (.ShiftIn(A), .ShiftBit(ShiftBit), .ShiftOut(shiftleft_1_shiftout));
  ShiftRight shiftright_1 (.ShiftBit(ShiftBit), .ShiftIn(A), .ShiftOut(shiftright_1_shiftout));
  AddSub addsub_1 (.sub(SubSelect), .B(B), .A(A), .result(addsub_1_result));  // open: ovf
  Multiplexer #(.select(3), .width(16), .enable("false")) multiplexer_1 (
    .in0(addsub_1_result), .in1(shiftleft_1_shiftout), .in2(shiftright_1_shiftout), .in3(and_1_out),
    .in4(not_1_out), .out(ALUOut), .sel(ALUop));  // open: in5, in6, in7
endmodule

module AddSub (
  input  sub,
  input  [15:0] B,
  input  [15:0] A,
  output [15:0] result,
  output ovf
);

  wire onebitadd_1_cout, onebitadd_2_cout, onebitadd_3_cout, onebitadd_4_cout, onebitadd_5_cout,
       onebitadd_6_cout, onebitadd_7_cout, onebitadd_8_cout, onebitadd_9_cout, onebitadd_10_cout,
       onebitadd_11_cout, onebitadd_12_cout, onebitadd_13_cout, onebitadd_14_cout, onebitadd_15_cout,
       onebitadd_16_cout, xor_2_out, xor_3_out, xor_4_out, xor_5_out, xor_6_out, xor_7_out, xor_8_out,
       xor_9_out, xor_10_out, xor_11_out, xor_12_out, xor_13_out, xor_14_out, xor_15_out, xor_16_out,
       xor_17_out;

  xor xor_1 (ovf, onebitadd_2_cout, onebitadd_1_cout);
  xor xor_2 (xor_2_out, sub, B[15]);
  xor xor_3 (xor_3_out, sub, B[14]);
  OneBitAdd onebitadd_1 (
    .Cin(onebitadd_2_cout), .A(A[15]), .result(result[15]), .B(xor_2_out), .Cout(onebitadd_1_cout));
  xor xor_4 (xor_4_out, sub, B[13]);
  OneBitAdd onebitadd_2 (
    .Cin(onebitadd_3_cout), .A(A[14]), .result(result[14]), .B(xor_3_out), .Cout(onebitadd_2_cout));
  OneBitAdd onebitadd_3 (
    .Cin(onebitadd_4_cout), .A(A[13]), .result(result[13]), .B(xor_4_out), .Cout(onebitadd_3_cout));
  xor xor_5 (xor_5_out, sub, B[12]);
  xor xor_6 (xor_6_out, sub, B[11]);
  OneBitAdd onebitadd_4 (
    .Cin(onebitadd_5_cout), .A(A[12]), .result(result[12]), .B(xor_5_out), .Cout(onebitadd_4_cout));
  xor xor_7 (xor_7_out, sub, B[10]);
  OneBitAdd onebitadd_5 (
    .Cin(onebitadd_6_cout), .A(A[11]), .result(result[11]), .B(xor_6_out), .Cout(onebitadd_5_cout));
  xor xor_8 (xor_8_out, sub, B[9]);
  OneBitAdd onebitadd_6 (
    .Cin(onebitadd_7_cout), .A(A[10]), .result(result[10]), .B(xor_7_out), .Cout(onebitadd_6_cout));
  OneBitAdd onebitadd_7 (.Cin(onebitadd_8_cout), .A(A[9]), .result(result[9]), .B(xor_8_out), .Cout(onebitadd_7_cout));
  xor xor_9 (xor_9_out, sub, B[8]);
  xor xor_10 (xor_10_out, sub, B[7]);
  OneBitAdd onebitadd_8 (.Cin(onebitadd_9_cout), .A(A[8]), .result(result[8]), .B(xor_9_out), .Cout(onebitadd_8_cout));
  xor xor_11 (xor_11_out, sub, B[6]);
  OneBitAdd onebitadd_9 (
    .Cin(onebitadd_10_cout), .A(A[7]), .result(result[7]), .B(xor_10_out), .Cout(onebitadd_9_cout));
  xor xor_12 (xor_12_out, sub, B[5]);
  OneBitAdd onebitadd_10 (
    .Cin(onebitadd_11_cout), .A(A[6]), .result(result[6]), .B(xor_11_out), .Cout(onebitadd_10_cout));
  OneBitAdd onebitadd_11 (
    .Cin(onebitadd_12_cout), .A(A[5]), .result(result[5]), .B(xor_12_out), .Cout(onebitadd_11_cout));
  xor xor_13 (xor_13_out, sub, B[4]);
  xor xor_14 (xor_14_out, sub, B[3]);
  OneBitAdd onebitadd_12 (
    .Cin(onebitadd_13_cout), .A(A[4]), .result(result[4]), .B(xor_13_out), .Cout(onebitadd_12_cout));
  xor xor_15 (xor_15_out, sub, B[2]);
  OneBitAdd onebitadd_13 (
    .Cin(onebitadd_14_cout), .A(A[3]), .result(result[3]), .B(xor_14_out), .Cout(onebitadd_13_cout));
  xor xor_16 (xor_16_out, sub, B[1]);
  OneBitAdd onebitadd_14 (
    .Cin(onebitadd_15_cout), .A(A[2]), .result(result[2]), .B(xor_15_out), .Cout(onebitadd_14_cout));
  OneBitAdd onebitadd_15 (
    .Cin(onebitadd_16_cout), .A(A[1]), .result(result[1]), .B(xor_16_out), .Cout(onebitadd_15_cout));
  xor xor_17 (xor_17_out, sub, B[0]);
  OneBitAdd onebitadd_16 (.Cin(sub), .A(A[0]), .result(result[0]), .B(xor_17_out), .Cout(onebitadd_16_cout));
endmodule

module OneBitAdd (
  input  Cin,
  input  A,
  input  B,
  output result,
  output Cout
);

  wire and_1_out, and_2_out, xor_1_out;

  and and_1 (and_1_out, B, A);
  xor xor_1 (xor_1_out, A, B);
  or or_1 (Cout, and_1_out, and_2_out);
  and and_2 (and_2_out, xor_1_out, Cin);
  xor xor_2 (result, Cin, xor_1_out);
endmodule

module ShiftLeft (
  input  [15:0] ShiftIn,
  input  [2:0] ShiftBit,
  output [15:0] ShiftOut
);

  wire multiplexer_1_out, multiplexer_2_out, multiplexer_3_out, multiplexer_4_out, multiplexer_5_out,
       multiplexer_6_out, multiplexer_7_out, multiplexer_8_out, multiplexer_9_out, multiplexer_10_out,
       multiplexer_11_out, multiplexer_12_out, multiplexer_13_out, multiplexer_14_out, multiplexer_15_out,
       multiplexer_16_out, multiplexer_17_out, multiplexer_18_out, multiplexer_19_out, multiplexer_20_out,
       multiplexer_21_out, multiplexer_22_out, multiplexer_23_out, multiplexer_24_out, multiplexer_25_out,
       multiplexer_26_out, multiplexer_27_out, multiplexer_28_out, multiplexer_29_out, multiplexer_30_out,
       multiplexer_31_out, multiplexer_32_out;

  Multiplexer #(.enable("false")) multiplexer_1 (
    .in0(ShiftIn[0]), .in1(1'b0), .out(multiplexer_1_out), .sel(ShiftBit[2]));
  Multiplexer #(.enable("false")) multiplexer_2 (
    .in0(ShiftIn[1]), .in1(1'b0), .out(multiplexer_2_out), .sel(ShiftBit[2]));
  Multiplexer #(.enable("false")) multiplexer_3 (
    .in0(ShiftIn[2]), .in1(1'b0), .out(multiplexer_3_out), .sel(ShiftBit[2]));
  Multiplexer #(.enable("false")) multiplexer_4 (
    .in0(ShiftIn[3]), .in1(1'b0), .out(multiplexer_4_out), .sel(ShiftBit[2]));
  Multiplexer #(.enable("false")) multiplexer_5 (
    .in0(ShiftIn[4]), .in1(ShiftIn[0]), .out(multiplexer_5_out), .sel(ShiftBit[2]));
  Multiplexer #(.enable("false")) multiplexer_6 (
    .in0(ShiftIn[5]), .in1(ShiftIn[1]), .out(multiplexer_6_out), .sel(ShiftBit[2]));
  Multiplexer #(.enable("false")) multiplexer_7 (
    .in0(ShiftIn[6]), .in1(ShiftIn[2]), .out(multiplexer_7_out), .sel(ShiftBit[2]));
  Multiplexer #(.enable("false")) multiplexer_8 (
    .in0(ShiftIn[7]), .in1(ShiftIn[3]), .out(multiplexer_8_out), .sel(ShiftBit[2]));
  Multiplexer #(.enable("false")) multiplexer_9 (
    .in0(ShiftIn[8]), .in1(ShiftIn[4]), .out(multiplexer_9_out), .sel(ShiftBit[2]));
  Multiplexer #(.enable("false")) multiplexer_10 (
    .in0(ShiftIn[9]), .in1(ShiftIn[5]), .out(multiplexer_10_out), .sel(ShiftBit[2]));
  Multiplexer #(.enable("false")) multiplexer_11 (
    .in0(ShiftIn[10]), .in1(ShiftIn[6]), .out(multiplexer_11_out), .sel(ShiftBit[2]));
  Multiplexer #(.enable("false")) multiplexer_12 (
    .in0(ShiftIn[11]), .in1(ShiftIn[7]), .out(multiplexer_12_out), .sel(ShiftBit[2]));
  Multiplexer #(.enable("false")) multiplexer_13 (
    .in0(ShiftIn[12]), .in1(ShiftIn[8]), .out(multiplexer_13_out), .sel(ShiftBit[2]));
  Multiplexer #(.enable("false")) multiplexer_14 (
    .in0(ShiftIn[13]), .in1(ShiftIn[9]), .out(multiplexer_14_out), .sel(ShiftBit[2]));
  Multiplexer #(.enable("false")) multiplexer_15 (
    .in0(ShiftIn[14]), .in1(ShiftIn[10]), .out(multiplexer_15_out), .sel(ShiftBit[2]));
  Multiplexer #(.enable("false")) multiplexer_16 (
    .in0(ShiftIn[15]), .in1(ShiftIn[11]), .out(multiplexer_16_out), .sel(ShiftBit[2]));
  Multiplexer #(.enable("false")) multiplexer_17 (
    .in0(multiplexer_1_out), .in1(1'b0), .out(multiplexer_17_out), .sel(ShiftBit[1]));
  Multiplexer #(.enable("false")) multiplexer_18 (
    .in0(multiplexer_2_out), .in1(1'b0), .out(multiplexer_18_out), .sel(ShiftBit[1]));
  Multiplexer #(.enable("false")) multiplexer_19 (
    .in0(multiplexer_3_out), .in1(multiplexer_1_out), .out(multiplexer_19_out), .sel(ShiftBit[1]));
  Multiplexer #(.enable("false")) multiplexer_20 (
    .in0(multiplexer_4_out), .in1(multiplexer_2_out), .out(multiplexer_20_out), .sel(ShiftBit[1]));
  Multiplexer #(.enable("false")) multiplexer_21 (
    .in0(multiplexer_5_out), .in1(multiplexer_3_out), .out(multiplexer_21_out), .sel(ShiftBit[1]));
  Multiplexer #(.enable("false")) multiplexer_22 (
    .in0(multiplexer_6_out), .in1(multiplexer_4_out), .out(multiplexer_22_out), .sel(ShiftBit[1]));
  Multiplexer #(.enable("false")) multiplexer_23 (
    .in0(multiplexer_7_out), .in1(multiplexer_5_out), .out(multiplexer_23_out), .sel(ShiftBit[1]));
  Multiplexer #(.enable("false")) multiplexer_24 (
    .in0(multiplexer_8_out), .in1(multiplexer_6_out), .out(multiplexer_24_out), .sel(ShiftBit[1]));
  Multiplexer #(.enable("false")) multiplexer_25 (
    .in0(multiplexer_9_out), .in1(multiplexer_7_out), .out(multiplexer_25_out), .sel(ShiftBit[1]));
  Multiplexer #(.enable("false")) multiplexer_26 (
    .in0(multiplexer_10_out), .in1(multiplexer_8_out), .out(multiplexer_26_out), .sel(ShiftBit[1]));
  Multiplexer #(.enable("false")) multiplexer_27 (
    .in0(multiplexer_11_out), .in1(multiplexer_9_out), .out(multiplexer_27_out), .sel(ShiftBit[1]));
  Multiplexer #(.enable("false")) multiplexer_28 (
    .in0(multiplexer_12_out), .in1(multiplexer_10_out), .out(multiplexer_28_out), .sel(ShiftBit[1]));
  Multiplexer #(.enable("false")) multiplexer_29 (
    .in0(multiplexer_13_out), .in1(multiplexer_11_out), .out(multiplexer_29_out), .sel(ShiftBit[1]));
  Multiplexer #(.enable("false")) multiplexer_30 (
    .in0(multiplexer_14_out), .in1(multiplexer_12_out), .out(multiplexer_30_out), .sel(ShiftBit[1]));
  Multiplexer #(.enable("false")) multiplexer_31 (
    .in0(multiplexer_15_out), .in1(multiplexer_13_out), .out(multiplexer_31_out), .sel(ShiftBit[1]));
  Multiplexer #(.enable("false")) multiplexer_32 (
    .in0(multiplexer_16_out), .in1(multiplexer_14_out), .out(multiplexer_32_out), .sel(ShiftBit[1]));
  Multiplexer #(.enable("false")) multiplexer_33 (
    .in0(multiplexer_17_out), .in1(1'b0), .out(ShiftOut[0]), .sel(ShiftBit[0]));
  Multiplexer #(.enable("false")) multiplexer_34 (
    .in0(multiplexer_18_out), .in1(multiplexer_17_out), .out(ShiftOut[1]), .sel(ShiftBit[0]));
  Multiplexer #(.enable("false")) multiplexer_35 (
    .in0(multiplexer_19_out), .in1(multiplexer_18_out), .out(ShiftOut[2]), .sel(ShiftBit[0]));
  Multiplexer #(.enable("false")) multiplexer_36 (
    .in0(multiplexer_20_out), .in1(multiplexer_19_out), .out(ShiftOut[3]), .sel(ShiftBit[0]));
  Multiplexer #(.enable("false")) multiplexer_37 (
    .in0(multiplexer_21_out), .in1(multiplexer_20_out), .out(ShiftOut[4]), .sel(ShiftBit[0]));
  Multiplexer #(.enable("false")) multiplexer_38 (
    .in0(multiplexer_22_out), .in1(multiplexer_21_out), .out(ShiftOut[5]), .sel(ShiftBit[0]));
  Multiplexer #(.enable("false")) multiplexer_39 (
    .in0(multiplexer_23_out), .in1(multiplexer_22_out), .out(ShiftOut[6]), .sel(ShiftBit[0]));
  Multiplexer #(.enable("false")) multiplexer_40 (
    .in0(multiplexer_24_out), .in1(multiplexer_23_out), .out(ShiftOut[7]), .sel(ShiftBit[0]));
  Multiplexer #(.enable("false")) multiplexer_41 (
    .in0(multiplexer_25_out), .in1(multiplexer_24_out), .out(ShiftOut[8]), .sel(ShiftBit[0]));
  Multiplexer #(.enable("false")) multiplexer_42 (
    .in0(multiplexer_26_out), .in1(multiplexer_25_out), .out(ShiftOut[9]), .sel(ShiftBit[0]));
  Multiplexer #(.enable("false")) multiplexer_43 (
    .in0(multiplexer_27_out), .in1(multiplexer_26_out), .out(ShiftOut[10]), .sel(ShiftBit[0]));
  Multiplexer #(.enable("false")) multiplexer_44 (
    .in0(multiplexer_28_out), .in1(multiplexer_27_out), .out(ShiftOut[11]), .sel(ShiftBit[0]));
  Multiplexer #(.enable("false")) multiplexer_45 (
    .in0(multiplexer_29_out), .in1(multiplexer_28_out), .out(ShiftOut[12]), .sel(ShiftBit[0]));
  Multiplexer #(.enable("false")) multiplexer_46 (
    .in0(multiplexer_30_out), .in1(multiplexer_29_out), .out(ShiftOut[13]), .sel(ShiftBit[0]));
  Multiplexer #(.enable("false")) multiplexer_47 (
    .in0(multiplexer_31_out), .in1(multiplexer_30_out), .out(ShiftOut[14]), .sel(ShiftBit[0]));
  Multiplexer #(.enable("false")) multiplexer_48 (
    .in0(multiplexer_32_out), .in1(multiplexer_31_out), .out(ShiftOut[15]), .sel(ShiftBit[0]));

  // Other names for the same wires on the sheet: SBit0 = ShiftBit[0]; SBit1 = ShiftBit[1]; SBit2 = ShiftBit[2];
  //   b0 = ShiftIn[0]; b1 = ShiftIn[1]; b2 = ShiftIn[2]; b3 = ShiftIn[3]; b4 = ShiftIn[4]; b5 = ShiftIn[5];
  //   b6 = ShiftIn[6]; b7 = ShiftIn[7]; b8 = ShiftIn[8]; b9 = ShiftIn[9]; b10 = ShiftIn[10]; b11 = ShiftIn[11];
  //   b12 = ShiftIn[12]; b13 = ShiftIn[13]; b14 = ShiftIn[14]; b15 = ShiftIn[15]
endmodule

module ShiftRight (
  input  [2:0] ShiftBit,
  input  [15:0] ShiftIn,
  output [15:0] ShiftOut
);

  ShiftLeft shiftleft_1 (
    .ShiftIn({ShiftIn[0], ShiftIn[1], ShiftIn[2], ShiftIn[3], ShiftIn[4], ShiftIn[5], ShiftIn[6], ShiftIn[7], ShiftIn[8], ShiftIn[9], ShiftIn[10], ShiftIn[11], ShiftIn[12], ShiftIn[13], ShiftIn[14], ShiftIn[15]}),
    .ShiftBit(ShiftBit),
    .ShiftOut({ShiftOut[0], ShiftOut[1], ShiftOut[2], ShiftOut[3], ShiftOut[4], ShiftOut[5], ShiftOut[6], ShiftOut[7], ShiftOut[8], ShiftOut[9], ShiftOut[10], ShiftOut[11], ShiftOut[12], ShiftOut[13], ShiftOut[14], ShiftOut[15]}));
endmodule

module Control (
  input  [3:0] Opcode,
  output AddOrSub,
  output Rwe,
  output ALUinB,
  output bne,
  output ble,
  output Rdst,
  output JP,
  output [2:0] ALUOp,
  output Jre,
  output Jale,
  output InE,
  output OutE,
  output Rwd,
  output DMwe
);

  wire Add, Addi, Ander, lw, Noter, or_1_out, ShiftLeft, ShiftRight;

  Decoder #(.select(4)) decoder_1 (
    .out0(Add), .out1(Addi), .out2(AddOrSub), .out3(ShiftLeft), .out4(ShiftRight), .out5(Ander),
    .out6(Noter), .out7(lw), .out8(DMwe), .out9(bne), .out10(ble), .out11(JP), .out12(Jre), .out13(Jale),
    .out14(InE), .out15(OutE), .sel(Opcode));  // open: en
  or or_1 (or_1_out, Add, lw, Addi, DMwe, AddOrSub);
  assign ALUOp = or_1_out ? 3'b000 : 3'bz;  // Controlled_Buffer controlled_buffer_1
  or or_2 (ALUinB, Addi, lw, ShiftRight, DMwe, ShiftLeft);
  assign ALUOp = ShiftLeft ? 3'b001 : 3'bz;  // Controlled_Buffer controlled_buffer_2
  assign ALUOp = ShiftRight ? 3'b010 : 3'bz;  // Controlled_Buffer controlled_buffer_3
  assign ALUOp = Ander ? 3'b011 : 3'bz;  // Controlled_Buffer controlled_buffer_4
  assign ALUOp = Noter ? 3'b100 : 3'bz;  // Controlled_Buffer controlled_buffer_5
  or or_3 (Rwe, Ander, Jale, lw, Addi, AddOrSub, ShiftRight, ShiftLeft, Add, InE, Noter);
  or or_4 (Rdst, Ander, Add, ShiftLeft, ShiftRight, AddOrSub, Noter);
  buf or_5 (Rwd, lw);  // OR_Gate

  // Other names for the same wires on the sheet: Inp = InE; j = JP; jal = Jale; jr = Jre; Outp = OutE; Sub = AddOrSub;
  //   sw = DMwe
endmodule

module InstructionDecoder (
  input  [15:0] InstructionIn,
  output [3:0] Opcode,
  output [2:0] Rs,
  output [2:0] Rt,
  output [11:0] Address,
  output [2:0] Rd,
  output [5:0] Imm,
  output [2:0] Shamt
);


  assign Address = InstructionIn[11:0];
  assign Imm = InstructionIn[5:0];
  assign Opcode = InstructionIn[15:12];
  assign Rd = InstructionIn[5:3];
  assign Rs = InstructionIn[11:9];
  assign Rt = InstructionIn[8:6];
  assign Shamt = InstructionIn[2:0];

  // Other names for the same wires on the sheet: b15 = InstructionIn[0]; b14 = InstructionIn[1];
  //   b13 = InstructionIn[2]; b12 = InstructionIn[3]; b11 = InstructionIn[4]; b10 = InstructionIn[5];
  //   b9 = InstructionIn[6]; b8 = InstructionIn[7]; b7 = InstructionIn[8]; b6 = InstructionIn[9];
  //   b5 = InstructionIn[10]; b4 = InstructionIn[11]; b3 = InstructionIn[12]; b2 = InstructionIn[13];
  //   b1 = InstructionIn[14]; b0 = InstructionIn[15]
endmodule

module PCAdder (
  input  [15:0] PCin,
  output [15:0] PCout
);

  AddSub addsub_1 (.sub(1'b0), .B(16'h1), .A(PCin), .result(PCout));  // open: ovf
endmodule

module memory_latch (
  input  [15:0] address,
  input  WE,
  input  clk,
  input  [15:0] data_in,
  output [15:0] address_latched,
  output WE_latched,
  output OE_latched,
  output [15:0] data_in_latched
);

  wire DMwe_latch_q;
  wire [15:0] addr_latch_q;

  Register #(.width(16), .trigger("falling")) addr_latch (
    .D(address), .en(WE), .clk(clk), .Q(addr_latch_q));  // open: clr
  D_Flip_Flop #(.trigger("falling")) DMwe_latch (.D(WE), .clk(clk), .Q(DMwe_latch_q));  // open: Qn, preset, reset
  Register #(.width(16), .trigger("falling")) data_to_be_written (
    .D(data_in), .en(WE), .clk(clk), .Q(data_in_latched));  // open: clr
  Multiplexer #(.width(16), .enable("false")) multiplexer_1 (
    .in0(address), .in1(addr_latch_q), .out(address_latched), .sel(DMwe_latch_q));
  and and_1 (WE_latched, clk, DMwe_latch_q);
  not not_1 (OE_latched, WE_latched);
endmodule

module NotEqualTo (
  input  [15:0] B,
  input  [15:0] A,
  output NotEqual
);

  wire [1:0] or_3_out;
  wire [3:0] or_2_out;
  wire [7:0] or_1_out;
  wire [15:0] addsub_1_result;

  AddSub addsub_1 (.sub(1'b1), .B(B), .A(A), .result(addsub_1_result));  // open: ovf
  assign or_1_out = addsub_1_result[7:0] | addsub_1_result[15:8];  // OR_Gate or_1, 8 bits wide
  assign or_2_out = or_1_out[3:0] | or_1_out[7:4];  // OR_Gate or_2, 4 bits wide
  assign or_3_out = or_2_out[1:0] | or_2_out[3:2];  // OR_Gate or_3, 2 bits wide
  or or_4 (NotEqual, or_3_out[0], or_3_out[1]);
endmodule

module LessThan (
  input  [15:0] B,
  input  [15:0] A,
  output Neg
);

  wire not_1_out, notequalto_1_notequal;
  wire [15:0] addsub_1_result;

  AddSub addsub_1 (.sub(1'b1), .B(B), .A(A), .result(addsub_1_result));  // open: ovf
  // Probe on addsub_1_result
  // Probe on addsub_1_result[15]
  NotEqualTo notequalto_1 (.NotEqual(notequalto_1_notequal), .B(B), .A(A));
  not not_1 (not_1_out, notequalto_1_notequal);
  or or_1 (Neg, addsub_1_result[15], not_1_out);
endmodule

module IO (
  input  clk,
  input  [15:0] RegData,
  input  ReadEnable,
  input  WriteEnable,
  input  Reset,
  output [15:0] KeyboardOut
);

  wire keyboard_1_avail;
  wire [6:0] bit_extender_1_out;

  Keyboard keyboard_1 (.clk(clk), .re(ReadEnable), .clr(Reset), .avail(keyboard_1_avail), .data(KeyboardOut[6:0]));
  not not_1 (KeyboardOut[7], keyboard_1_avail);
  Bit_Extender #(.in_width(16), .out_width(7)) bit_extender_1 (.in(RegData), .out(bit_extender_1_out));
  TTY #(.rows(13), .cols(80)) tty_1 (.data(bit_extender_1_out), .clk(clk), .we(WriteEnable), .clr(Reset));

  assign KeyboardOut[15:8] = {8{1'b0}};
endmodule
